# Fritzing sketch waterrocket_promini (saved by Fritzing 0.9.3b)
circuit board: 8.46667cm x 5.64444cm
breadboards: 1

parts:
  R1 = Resistor [tolerance=±5% resistance=220 package=THT]
  LED1 = LED - 5mm [color="Red (633nm)" package="5 mm [THT]"]
  S1 = Pushbutton [package="[THT]"]
  S2 = Toggle Switch [package=THT]
  Onderdeel1 = 10DOF L3GD20 LSM303D BMP180
  J1 = Basic Servo
  SD_card_module1 = SD Card Module
  Onderdeel3 = Arduino Pro Mini v13

nets:
  N1: R1.Pin_0, Onderdeel3.D9_PWM
  N2: R1.Pin_1, LED1.anode
  GND: LED1.cathode, S1.Pin_3, S1.Pin_4, S2.COM, Onderdeel1.GND, J1.gnd, SD_card_module1.GND, Onderdeel3.GND
  N3: S1.Pin_1, S1.Pin_2, Onderdeel3.D7
  N4: S2.L2, Onderdeel3.D8
  VCC: Onderdeel1.3V3, J1.vcc, SD_card_module1.3.3V, Onderdeel3.VCC
  N5: Onderdeel1.SCL, Onderdeel3.A5
  N6: Onderdeel1.SDA, Onderdeel3.A4
  N7: J1.pulse, Onderdeel3.A0
  N8: SD_card_module1.MISO#4, Onderdeel3.D12/MISO
  N9: SD_card_module1.SCK, Onderdeel3.D13/SCK
  N10: SD_card_module1.MISO#6, Onderdeel3.D11_PWM/MOSI
  N11: SD_card_module1.CS, Onderdeel3.D10_PWM/SS

custom parts:
  10DOF L3GD20 LSM303D BMP180: Dimensions: 22 mm × 17 mm Operating voltage: 2.5 V to 5.5 V Supply current: 8mA Output format (I2C/SPI): Gyro: one 16-bit reading per axis Accelerometer: one 16-bit reading per axis Magnetometer: one 16-bit reading per axis Barometer: 24-bit pressure reading (I2C only) Gyro: ±245, ±500, or ±2000°/s Accelerometer: ±2, ±4, ±6, ±8, or ±16 g Magnetometer: ±2, ±4, ±8, or ±12 gauss Barometer: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
  SD Card Module: SD Card Module Slot Socket Reader For Arduino ARM MCU
